# Fritzing sketch circuit (saved by Fritzing 0.9.2b)
breadboards: 1

parts:
  Part1 = Spark Core (v1.0)
  R1 = Resistor [tolerance=±5% resistance=4.7k package=THT]
  R2 = Resistor [tolerance=±5% resistance=4.7k package=THT]
  J1 = Piezo Speaker
  R3 = Resistor [tolerance=±5% resistance=4.7k package=THT]

nets:
  N1: Part1.A0, J1.pin2
  N2: Part1.GND, J1.pin1
  N3: Part1.VIN, R1.Pin_1, R2.Pin_1
  N4: Part1.D0, R1.Pin_0
  N5: Part1.D1, R2.Pin_0
  N6: Part1.D2, R3.Pin_1
  N7: Part1.3V3, R3.Pin_0

notes:
  To DS18B20
  To LCD
